# Fritzing sketch switch2Pots (saved by Fritzing 0.9.0b)
breadboards: 1

parts:
  Switch = Pushbutton [package="[THT]"]
  Arudino_5V = Arduino Uno (Rev3)
  Potentiometer_1 = Rotary Potentiometer (Small) [maximum_resistance=100kΩ package=THT]
  Potentiometer_2 = Rotary Potentiometer (Small) [maximum_resistance=100kΩ package=THT]
  Resistor_(Fixed) = Resistor [tolerance=±5% resistance=10k package=THT]

nets:
  N1: Switch.Pin_1, Switch.Pin_2, Arudino_5V.D2, Resistor_(Fixed).Pin_0
  N2: Switch.Pin_3, Switch.Pin_4, Arudino_5V.5V, Potentiometer_1.leg2, Potentiometer_2.leg2
  N3: Arudino_5V.A0, Potentiometer_1.wiper
  N4: Arudino_5V.A1, Potentiometer_2.wiper
  GND: Arudino_5V.GND, Potentiometer_1.leg1, Potentiometer_2.leg1, Resistor_(Fixed).Pin_1
